# Fritzing sketch finalschematic (saved by Fritzing 0.9.3b)
breadboards: 1

parts:
  U1 = atmega328 [package=dip]
  Part1 = FTDI Basic Programmer
  SparkFun_Particle_Sensor_Breakout_-_MAX1 = SparkFun MAX30105_Breakout [part_number=SEN-14045]  # not connected

nets:
  N1: U1.D0_(RX), Part1.TXO
  N2: U1.D1_(TX), Part1.RXI
  5V: U1.VCC, Part1.POWER
  GND: U1.GND, Part1.GND

custom parts:
  SparkFun MAX30105_Breakout: Description: The SparkFun MAX30105 Particle Sensor is a flexible, powerful sensor enabling sensing of distance, heart rate, particle detection and even the blinking of an eye. The MAX30105 has been equipped with three LEDs as well as a very sensitive photon detector. The idea is to pulse the different LEDs, then detect what shines back. Based on the reflected signature it’s possible to detect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
